// Digital circuit D0.dig as structural Verilog
module D0 (
  input  Q2,
  input  Q1,
  input  Q0,
  input  X1,
  input  X0,
  output D0
);

  wire not_1_out, not_2_out, not_3_out, not_4_out, not_5_out, or_1_out, or_2_out, or_3_out;

  not not_1 (not_1_out, Q2);
  not not_2 (not_2_out, Q1);
  not not_3 (not_3_out, Q0);
  not not_4 (not_4_out, X1);
  not not_5 (not_5_out, X0);
  or or_1 (or_1_out, Q2, not_3_out, X1, X0);
  or or_2 (or_2_out, not_2_out, X1, not_5_out);
  or or_3 (or_3_out, not_1_out, not_3_out, not_4_out);
  and and_1 (D0, or_1_out, or_2_out, or_3_out);
endmodule
