// Digital circuit D1.dig as structural Verilog
module D1 (
  input  Q2,
  input  Q1,
  input  Q0,
  input  X1,
  input  X0,
  output D1
);

  wire and_1_out, and_2_out, and_3_out, not_1_out, not_2_out, not_3_out, not_4_out, not_5_out;

  not not_1 (not_1_out, Q2);
  not not_2 (not_2_out, Q1);
  not not_3 (not_3_out, Q0);
  not not_4 (not_4_out, X1);
  not not_5 (not_5_out, X0);
  and and_1 (and_1_out, not_1_out, not_2_out, Q0, not_4_out);
  and and_2 (and_2_out, not_1_out, Q0, X0);
  and and_3 (and_3_out, Q1, not_3_out, not_4_out, not_5_out);
  or or_1 (D1, and_1_out, and_2_out, and_3_out);
endmodule
