// Digital circuit solucio.dig as structural Verilog
module solucio (
  input  X1,
  input  X0,
  input  clk,
  output VERD,
  output VERMELL,
  output GROC,
  output BLAU
);

  wire and_1_out, and_2_out, and_3_out, and_4_out, d0_1_d0, D0_2_nq, D0_2_q, d1_1_d1, D1_2_nq, D1_2_q,
       d2_1_d2, D2_2_nq, not_1_out, not_2_out;

  not not_1 (not_1_out, X1);
  not not_2 (not_2_out, X0);
  D2 d2_1 (.Q2(BLAU), .Q1(D1_2_q), .Q0(D0_2_q), .X1(X1), .X0(X0), .D2(d2_1_d2));
  D1 d1_1 (.Q2(BLAU), .Q1(D1_2_q), .Q0(D0_2_q), .X1(X1), .X0(X0), .D1(d1_1_d1));
  D0 d0_1 (.Q2(BLAU), .Q1(D1_2_q), .Q0(D0_2_q), .X1(X1), .X0(X0), .D0(d0_1_d0));
  D_FF D2_2 (.D(d2_1_d2), .C(clk), .Q(BLAU), .nQ(D2_2_nq));
  D_FF D1_2 (.D(d1_1_d1), .C(clk), .Q(D1_2_q), .nQ(D1_2_nq));
  D_FF D0_2 (.D(d0_1_d0), .C(clk), .Q(D0_2_q), .nQ(D0_2_nq));
  and and_1 (and_1_out, D1_2_q, D0_2_nq);
  and and_2 (and_2_out, BLAU, D0_2_q);
  and and_3 (and_3_out, D1_2_q, D0_2_q);
  and and_4 (and_4_out, BLAU, D0_2_q);
  and and_5 (VERD, D1_2_nq, D0_2_q);
  or or_1 (VERMELL, and_1_out, and_2_out);
  or or_2 (GROC, and_3_out, and_4_out);
  LED LED_VERD (.in(VERD));
  LED LED_VERMELL (.in(VERMELL));
  LED LED_GROC (.in(GROC));
  LED LED_BLAU (.in(BLAU));
endmodule
